// Logisim project registro_bidireccional.circ as structural Verilog: 1 circuit, main circuit main
module main (
  input  CLK,
  input  R_L,
  input  I0,
  input  RST,
  output O0,
  output O1,
  output O2,
  output O3
);

  wire and_1_out, and_2_out, and_3_out, and_4_out, and_5_out, and_6_out, and_7_out, and_8_out, not_1_out,
       not_2_out, not_3_out, not_4_out, or_1_out, or_2_out, or_3_out, or_4_out;

  and and_1 (and_1_out, I0, R_L);
  or or_1 (or_1_out, and_1_out, and_2_out);
  and and_2 (and_2_out, not_1_out, O1);
  not not_1 (not_1_out, R_L);
  D_Flip_Flop d_ff_1 (.clk(CLK), .D(or_1_out), .Q(O0), .reset(RST));  // open: Qn, preset, en
  or or_2 (or_2_out, and_3_out, and_4_out);
  and and_3 (and_3_out, O0, R_L);
  D_Flip_Flop d_ff_2 (.clk(CLK), .D(or_2_out), .Q(O1), .reset(RST));  // open: Qn, preset, en
  and and_4 (and_4_out, not_2_out, O2);
  not not_2 (not_2_out, R_L);
  or or_3 (or_3_out, and_5_out, and_7_out);
  and and_5 (and_5_out, O1, R_L);
  not not_3 (not_3_out, R_L);
  D_Flip_Flop d_ff_3 (.clk(CLK), .D(or_3_out), .Q(O2), .reset(RST));  // open: Qn, preset, en
  and and_6 (and_6_out, O2, R_L);
  and and_7 (and_7_out, not_3_out, O3);
  or or_4 (or_4_out, and_6_out, and_8_out);
  and and_8 (and_8_out, not_4_out, I0);
  not not_4 (not_4_out, R_L);
  D_Flip_Flop d_ff_4 (.clk(CLK), .D(or_4_out), .Q(O3), .reset(RST));  // open: Qn, preset, en

  // Other names for the same wires on the sheet: RL = R_L
endmodule
